// Digital circuit 8bit PC.dig as structural Verilog
module _8bit_PC (
  input  [1:0] CTRL,
  input  CLK,
  input  [7:0] Carry,
  output [7:0] C
);

  wire [7:0] _8bitaddder_1_p4, multiplexer_1_out;

  // _8Bitaddder _8bitaddder_1: pin names not known; wires that end beside it: C, Carry, 1'b0, _8bitaddder_1_p4
  Multiplexer #(.Selector_Bits(2), .Bits(8)) multiplexer_1 (
    .sel(CTRL), .in_0(C), .in_1(_8bitaddder_1_p4), .in_2({8{1'b0}}), .in_3({8{1'b1}}), .out(multiplexer_1_out));
  D_FF d_ff_1 (.D(multiplexer_1_out[7]), .C(CLK), .Q(C[7]));  // open: nQ
  D_FF d_ff_2 (.D(multiplexer_1_out[6]), .C(CLK), .Q(C[6]));  // open: nQ
  D_FF d_ff_3 (.D(multiplexer_1_out[5]), .C(CLK), .Q(C[5]));  // open: nQ
  D_FF d_ff_4 (.D(multiplexer_1_out[4]), .C(CLK), .Q(C[4]));  // open: nQ
  D_FF d_ff_5 (.D(multiplexer_1_out[3]), .C(CLK), .Q(C[3]));  // open: nQ
  D_FF d_ff_6 (.D(multiplexer_1_out[2]), .C(CLK), .Q(C[2]));  // open: nQ
  D_FF d_ff_7 (.D(multiplexer_1_out[1]), .C(CLK), .Q(C[1]));  // open: nQ
  D_FF d_ff_8 (.D(multiplexer_1_out[0]), .C(CLK), .Q(C[0]));  // open: nQ

  // Notes on the sheet:
  //   CTRL: 00->Load
  //   01->increment
  //   10->Clear
  //   11->Set FF
endmodule
