// Digital circuit 8bitGPR.dig as structural Verilog
module _8bitGPR (
  input  [1:0] Register_Select,
  input  [1:0] Ctrl,
  input  [7:0] \input ,
  input  CLK,
  output [7:0] Output
);

  wire and_1_out, and_2_out, and_3_out, and_4_out, decoder_1_out_0, decoder_1_out_1, decoder_1_out_2,
       decoder_1_out_3;
  wire [7:0] R0_p4, R1_p4, R2_p4, R3_p4;

  Decoder #(.Selector_Bits(2)) decoder_1 (
    .sel(Register_Select), .out_0(decoder_1_out_0), .out_1(decoder_1_out_1), .out_2(decoder_1_out_2),
    .out_3(decoder_1_out_3));
  and and_1 (and_1_out, decoder_1_out_0, CLK);
  and and_2 (and_2_out, decoder_1_out_1, CLK);
  and and_3 (and_3_out, decoder_1_out_2, CLK);
  and and_4 (and_4_out, CLK, decoder_1_out_3);
  // Register R0: pin names not known; wires that end beside it: \input , Ctrl, and_1_out, R0_p4
  // Register R1: pin names not known; wires that end beside it: \input , Ctrl, and_2_out, R1_p4
  // Register R2: pin names not known; wires that end beside it: \input , Ctrl, and_3_out, R2_p4
  // Register R3: pin names not known; wires that end beside it: \input , Ctrl, and_4_out, R3_p4
  Multiplexer #(.Selector_Bits(2), .Bits(8)) multiplexer_1 (
    .sel(Register_Select), .in_0(R0_p4), .in_1(R1_p4), .in_2(R2_p4), .in_3(R3_p4), .out(Output));
endmodule
