// Digital circuit IR.dig as structural Verilog
module IR (
  input  [7:0] data_in,
  input  LD,
  input  CLK,
  output [7:0] Data_out
);

  wire [7:0] multiplexer_1_out;

  Multiplexer #(.Bits(8)) multiplexer_1 (.sel(LD), .in_0(data_in), .in_1({8{1'b0}}), .out(multiplexer_1_out));
  Register #(.Bits(8)) IR (.D(multiplexer_1_out), .C(CLK), .en(LD), .Q(Data_out));
endmodule
