// Digital circuit SRAM.dig as structural Verilog
module SRAM (
  input  [3:0] Address,
  input  [7:0] Data_in,
  input  We,
  input  Cs,
  input  Oe,
  output [7:0] D_out
);

  RAMSinglePortSel #(.AddrBits(4), .Bits(8)) SRAM (.A(Address), .CS(Cs), .WE(We), .OE(Oe), .D(D_out));
endmodule
